// Logisim project project.circ as structural Verilog: 9 circuits, main circuit main
module main (
);

  wire ALUSrc, Branch, branch_taken, button_1_out, button_3_out, clk, clock_1_out, datamem_1_mw, Lt,
       multiplexer_1_out, not_1_out, not_2_out, reset, t_ff_1_q, undriven, undriven_2, undriven_3, zero;
  wire [2:0] funct3;
  wire [3:0] ALUop;
  wire [7:0] datamem_1_addr;
  wire [11:0] control_word;
  wire [31:0] alu_result, datamem_1_write_data_out, imm_b, imm_i, imm_j, imm_out, instruction, pc_1_pc_out,
       PC_plus_4, ram_1_dout, ram_read_data, rs1_val, rs2_val;

  PC pc_1 (
    .branch_taken(branch_taken), .jump(control_word[4]), .jalr(control_word[3]), .imm_b(imm_b),
    .imm_j(imm_j), .clk(clk), .reset(reset), .rs1_val(rs1_val), .imm_i(imm_i), .pc_out(pc_1_pc_out),
    .pc_plus_4(PC_plus_4));
  CU cu_1 (
    .instruction({instruction[31:15], funct3, instruction[11:0]}), .out_3(ALUop),
    .control_word({control_word[11:7], ALUSrc, Branch, control_word[4:0]}));  // open: in_2
  ROM #(.dataWidth(32)) InstMem (.addr(pc_1_pc_out[9:2]), .data({instruction[31:15], funct3, instruction[11:0]}));
  not not_1 (not_1_out, zero);
  not not_2 (not_2_out, Lt);
  RAM #(.asyncread("true"), .clearpin("true"), .dataWidth(32)) ram_1 (
    .addr(datamem_1_addr), .we(datamem_1_mw), .oe(undriven), .clk(undriven_2),
    .din(datamem_1_write_data_out), .dout(ram_1_dout), .clr(undriven_3));
  Multiplexer #(.select(3)) multiplexer_1 (
    .in0(zero), .in1(not_1_out), .in2(1'b0), .in3(1'b0), .in4(Lt), .in5(not_2_out), .in6(1'b0), .in7(1'b0),
    .out(multiplexer_1_out), .sel(funct3));
  and and_1 (branch_taken, multiplexer_1_out, Branch);
  DataMem datamem_1 (
    .funct3(funct3), .addr_in(alu_result), .mw({control_word[9], datamem_1_mw}),
    .MemRead({control_word[10], undriven}), .clk({clk, undriven_2}), .write_data(rs2_val),
    .Reset({reset, undriven_3}), .raw(ram_1_dout), .read_data(ram_read_data), .addr(datamem_1_addr),
    .write_data_out(datamem_1_write_data_out));  // open: raw_read_data
  // Probe on alu_result
  T_Flip_Flop t_ff_1 (.T(button_1_out), .clk(button_1_out), .Q(t_ff_1_q));  // open: Qn, reset, preset
  Button button_1 (.out(button_1_out));
  Button button_2 (.out(reset));
  Clock clock_1 (.out(clock_1_out));
  Multiplexer multiplexer_2 (.in0(clock_1_out), .in1(button_3_out), .out(clk), .sel(t_ff_1_q));
  Button button_3 (.out(button_3_out));
  // Probe on imm_out
  ImmGen immgen_1 (
    .imm_sel(control_word[2:0]), .instr({instruction[31:15], funct3, instruction[11:0]}), .type_b(imm_b),
    .type_i(imm_i), .type_j(imm_j), .imm_out(imm_out));
  RegFile regfile_1 (
    .rs2_index(instruction[24:20]), .rs1_index(instruction[19:15]), .ram_read_data(ram_read_data),
    .Pc_plus_4(PC_plus_4), .RegWrite(control_word[11]), .Reset(reset), .alu_result(alu_result),
    .rd_index(instruction[11:7]), .clk(clk), .MemtoReg(control_word[8:7]), .rs2_data(rs2_val),
    .rs1_data(rs1_val));
  // Probe on control_word[2:0]
  ALU alu_1 (
    .ALUop(ALUop), .ALUSrc(ALUSrc), .imm_out(imm_out), .rs2_val(rs2_val), .rs1_val(rs1_val),
    .Result(alu_result), .zero(zero), .Lt(Lt));  // open: Ltu

  // Other names for the same wires on the sheet: immSel[2:0] = control_word[2:0]; jalr = control_word[3];
  //   jal = control_word[4]; control_word[6:5] = {ALUSrc, Branch}; MemToReg[1:0] = control_word[8:7];
  //   MemWrite = control_word[9]; MemRead = control_word[10]; RegWrite = control_word[11];
  //   rd_index[4:0] = instruction[11:7]; instruction[14:12] = funct3; rs1_index[4:0] = instruction[19:15];
  //   rs2_index[4:0] = instruction[24:20]

  // Notes on the sheet:
  //   contents of InstMem (hex, n*v repeats v):
  //   93 100113 20a023 408093 110113 fe000ae3
  //   Control Word
  //   bit 11 (RegWrite)
  //   bit 10 (MemRead)
  //   bit 9 (MemWrite)
  //   bits 8..7 (MemToReg[1:0])
  //   bit 6 (ALUSrc)
  //   bit 5 (Branch)
  //   bit 4 (Jump(JAL))
  //   bit 3 (Jalr)
  //   bits 2..0 (ImmSel[2:0])
endmodule

module PC (
  input  [31:0] imm_b,
  input  [31:0] imm_j,
  input  [31:0] rs1_val,
  input  clk,
  input  [31:0] imm_i,
  input  reset,
  input  branch_taken,
  input  jump,
  input  jalr,
  output [31:0] pc_out,
  output [31:0] pc_plus_4
);

  wire [31:0] adder_1_out, adder_3_out, adder_4_out, and_1_out, multiplexer_1_out, multiplexer_2_out,
       multiplexer_3_out;

  Register #(.width(32)) pc_reg (.D(multiplexer_3_out), .en(1'b1), .clk(clk), .Q(pc_out), .clr(reset));
  Adder #(.width(32)) adder_1 (.a(rs1_val), .b(imm_i), .out(adder_1_out));  // open: cin, cout
  Adder #(.width(32)) adder_2 (.a(pc_out), .b(32'h4), .out(pc_plus_4));  // open: cin, cout
  Adder #(.width(32)) adder_3 (.a(pc_out), .b(imm_b), .out(adder_3_out));  // open: cin, cout
  Adder #(.width(32)) adder_4 (.a(pc_out), .b(imm_j), .out(adder_4_out));  // open: cin, cout
  assign and_1_out = adder_1_out & 32'hfffffffe;  // AND_Gate and_1, 32 bits wide
  Multiplexer #(.width(32)) multiplexer_1 (
    .in0(pc_plus_4), .in1(adder_3_out), .out(multiplexer_1_out), .sel(branch_taken));
  Multiplexer #(.width(32)) multiplexer_2 (
    .in0(multiplexer_1_out), .in1(adder_4_out), .out(multiplexer_2_out), .sel(jump));
  Multiplexer #(.width(32)) multiplexer_3 (
    .in0(multiplexer_2_out), .in1(and_1_out), .out(multiplexer_3_out), .sel(jalr));

  // Notes on the sheet:
  //   pc_next
endmodule

module InstMem (
  input  [7:0] in_1,
  output [31:0] out_2
);

  ROM #(.dataWidth(32)) rom_1 (.addr(in_1), .data(out_2));

  // Notes on the sheet:
  //   contents of rom_1 (hex, n*v repeats v):
  //   500093 a00113 2081b3 302023 2203
endmodule

module ImmGen (
  input  [31:0] instr,
  input  [2:0] imm_sel,
  output [31:0] type_i,
  output [31:0] imm_out,
  output [31:0] type_b,
  output [31:0] type_j
);

  wire [31:0] bit_extender_1_out;

  assign bit_extender_1_out = {{20{instr[31]}}, {instr[31:25], instr[11:7]}};  // Bit_Extender bit_extender_1
  assign type_i = {{20{instr[31]}}, instr[31:20]};  // Bit_Extender bit_extender_2
  assign type_b = {{19{instr[31]}}, {instr[31], instr[7], instr[30:25], instr[11:8], 1'b0}};  // Bit_Extender bit_extender_3
  assign type_j = {{11{instr[31]}}, {instr[31], instr[19:12], instr[20], instr[30:21], 1'b0}};  // Bit_Extender bit_extender_4
  Multiplexer #(.select(3), .width(32)) multiplexer_1 (
    .in0(type_i), .in1(bit_extender_1_out), .in2(type_b), .in3({instr[31:12], {12{1'b0}}}), .in4(type_j),
    .out(imm_out), .sel(imm_sel));  // open: in5, in6, in7

  // Other names for the same wires on the sheet: p11_8[3:0] = instr[11:8]; p7 = instr[7]; p30_21[9:0] = instr[30:21];
  //   p31_12[19:0] = instr[31:12]; p30_25[5:0] = instr[30:25]; p20 = instr[20]; p19_12[7:0] = instr[19:12];
  //   p31 = instr[31]; p0 = instr[0]

  // Notes on the sheet:
  //   type-s
  //   type-i
  //   type-B
  //   type-u
  //   type-j
endmodule

module RegFile (
  input  [31:0] alu_result,
  input  [31:0] ram_read_data,
  input  [31:0] Pc_plus_4,
  input  [1:0] MemtoReg,
  input  clk,
  input  RegWrite,
  input  Reset,
  input  [4:0] rd_index,
  input  [4:0] rs1_index,
  input  [4:0] rs2_index,
  output [31:0] rs1_data,
  output [31:0] rs2_data
);

  wire demultiplexer_1_out0, demultiplexer_1_out1, demultiplexer_1_out2, demultiplexer_1_out3;
  wire [7:0] demultiplexer_2_out0, demultiplexer_3_out0, demultiplexer_4_out0, demultiplexer_5_out0;
  wire [31:0] a0_q, a1_q, a2_q, a3_q, a4_q, a5_q, a6_q, a7_q, gp_q, ra_q, s0_q, s1_q, s2_q, s3_q, s4_q, s5_q,
       s6_q, s7_q, s8_q, s9_q, s10_q, s11_q, sp_q, t0_q, t1_q, t2_q, t3_q, t4_q, t5_q, t6_q, tp_q, write_data;

  Demultiplexer #(.select(2)) demultiplexer_1 (
    .out0(demultiplexer_1_out0), .out1(demultiplexer_1_out1), .out2(demultiplexer_1_out2),
    .out3(demultiplexer_1_out3), .in(RegWrite), .sel(rd_index[4:3]));
  Multiplexer #(.select(2), .width(32)) multiplexer_1 (
    .in0(alu_result), .in1(ram_read_data), .in2(Pc_plus_4), .in3({32{1'b0}}), .out(write_data), .sel(MemtoReg));
  // Probe on write_data
  Demultiplexer #(.select(3)) demultiplexer_2 (
    .out0(demultiplexer_2_out0[0]), .out1(demultiplexer_2_out0[1]), .out2(demultiplexer_2_out0[2]),
    .out3(demultiplexer_2_out0[3]), .out4(demultiplexer_2_out0[4]), .out5(demultiplexer_2_out0[5]),
    .out6(demultiplexer_2_out0[6]), .out7(demultiplexer_2_out0[7]), .in(demultiplexer_1_out0),
    .sel(rd_index[2:0]));
  Demultiplexer #(.select(3)) demultiplexer_3 (
    .out0(demultiplexer_3_out0[0]), .out1(demultiplexer_3_out0[1]), .out2(demultiplexer_3_out0[2]),
    .out3(demultiplexer_3_out0[3]), .out4(demultiplexer_3_out0[4]), .out5(demultiplexer_3_out0[5]),
    .out6(demultiplexer_3_out0[6]), .out7(demultiplexer_3_out0[7]), .in(demultiplexer_1_out1),
    .sel(rd_index[2:0]));
  Demultiplexer #(.select(3)) demultiplexer_4 (
    .out0(demultiplexer_4_out0[0]), .out1(demultiplexer_4_out0[1]), .out2(demultiplexer_4_out0[2]),
    .out3(demultiplexer_4_out0[3]), .out4(demultiplexer_4_out0[4]), .out5(demultiplexer_4_out0[5]),
    .out6(demultiplexer_4_out0[6]), .out7(demultiplexer_4_out0[7]), .in(demultiplexer_1_out2),
    .sel(rd_index[2:0]));
  Demultiplexer #(.select(3)) demultiplexer_5 (
    .out0(demultiplexer_5_out0[0]), .out1(demultiplexer_5_out0[1]), .out2(demultiplexer_5_out0[2]),
    .out3(demultiplexer_5_out0[3]), .out4(demultiplexer_5_out0[4]), .out5(demultiplexer_5_out0[5]),
    .out6(demultiplexer_5_out0[6]), .out7(demultiplexer_5_out0[7]), .in(demultiplexer_1_out3),
    .sel(rd_index[2:0]));
  Register #(.width(32)) s0 (.D(write_data), .en(demultiplexer_3_out0[0]), .clk(clk), .Q(s0_q), .clr(Reset));
  Register #(.width(32)) a6 (.D(write_data), .en(demultiplexer_4_out0[0]), .clk(clk), .Q(a6_q), .clr(Reset));
  Register #(.width(32)) s8 (.D(write_data), .en(demultiplexer_5_out0[0]), .clk(clk), .Q(s8_q), .clr(Reset));
  Register #(.width(32)) ra (.D(write_data), .en(demultiplexer_2_out0[1]), .clk(clk), .Q(ra_q), .clr(Reset));
  Register #(.width(32)) s1 (.D(write_data), .en(demultiplexer_3_out0[1]), .clk(clk), .Q(s1_q), .clr(Reset));
  Register #(.width(32)) a7 (.D(write_data), .en(demultiplexer_4_out0[1]), .clk(clk), .Q(a7_q), .clr(Reset));
  Register #(.width(32)) s9 (.D(write_data), .en(demultiplexer_5_out0[1]), .clk(clk), .Q(s9_q), .clr(Reset));
  Register #(.width(32)) sp (.D(write_data), .en(demultiplexer_2_out0[2]), .clk(clk), .Q(sp_q), .clr(Reset));
  Register #(.width(32)) a0 (.D(write_data), .en(demultiplexer_3_out0[2]), .clk(clk), .Q(a0_q), .clr(Reset));
  Register #(.width(32)) s2 (.D(write_data), .en(demultiplexer_4_out0[2]), .clk(clk), .Q(s2_q), .clr(Reset));
  Register #(.width(32)) s10 (.D(write_data), .en(demultiplexer_5_out0[2]), .clk(clk), .Q(s10_q), .clr(Reset));
  Register #(.width(32)) gp (.D(write_data), .en(demultiplexer_2_out0[3]), .clk(clk), .Q(gp_q), .clr(Reset));
  Register #(.width(32)) a1 (.D(write_data), .en(demultiplexer_3_out0[3]), .clk(clk), .Q(a1_q), .clr(Reset));
  Register #(.width(32)) s3 (.D(write_data), .en(demultiplexer_4_out0[3]), .clk(clk), .Q(s3_q), .clr(Reset));
  Register #(.width(32)) s11 (.D(write_data), .en(demultiplexer_5_out0[3]), .clk(clk), .Q(s11_q), .clr(Reset));
  Register #(.width(32)) tp (.D(write_data), .en(demultiplexer_2_out0[4]), .clk(clk), .Q(tp_q), .clr(Reset));
  Register #(.width(32)) a2 (.D(write_data), .en(demultiplexer_3_out0[4]), .clk(clk), .Q(a2_q), .clr(Reset));
  Register #(.width(32)) s4 (.D(write_data), .en(demultiplexer_4_out0[4]), .clk(clk), .Q(s4_q), .clr(Reset));
  Register #(.width(32)) t3 (.D(write_data), .en(demultiplexer_5_out0[4]), .clk(clk), .Q(t3_q), .clr(Reset));
  Register #(.width(32)) t0 (.D(write_data), .en(demultiplexer_2_out0[5]), .clk(clk), .Q(t0_q), .clr(Reset));
  Register #(.width(32)) a3 (.D(write_data), .en(demultiplexer_3_out0[5]), .clk(clk), .Q(a3_q), .clr(Reset));
  Register #(.width(32)) s5 (.D(write_data), .en(demultiplexer_4_out0[5]), .clk(clk), .Q(s5_q), .clr(Reset));
  Register #(.width(32)) t4 (.D(write_data), .en(demultiplexer_5_out0[5]), .clk(clk), .Q(t4_q), .clr(Reset));
  Register #(.width(32)) t1 (.D(write_data), .en(demultiplexer_2_out0[6]), .clk(clk), .Q(t1_q), .clr(Reset));
  Register #(.width(32)) a4 (.D(write_data), .en(demultiplexer_3_out0[6]), .clk(clk), .Q(a4_q), .clr(Reset));
  Register #(.width(32)) s6 (.D(write_data), .en(demultiplexer_4_out0[6]), .clk(clk), .Q(s6_q), .clr(Reset));
  Register #(.width(32)) t5 (.D(write_data), .en(demultiplexer_5_out0[6]), .clk(clk), .Q(t5_q), .clr(Reset));
  Register #(.width(32)) t2 (.D(write_data), .en(demultiplexer_2_out0[7]), .clk(clk), .Q(t2_q), .clr(Reset));
  Register #(.width(32)) a5 (.D(write_data), .en(demultiplexer_3_out0[7]), .clk(clk), .Q(a5_q), .clr(Reset));
  Register #(.width(32)) s7 (.D(write_data), .en(demultiplexer_4_out0[7]), .clk(clk), .Q(s7_q), .clr(Reset));
  Register #(.width(32)) t6 (.D(write_data), .en(demultiplexer_5_out0[7]), .clk(clk), .Q(t6_q), .clr(Reset));
  Multiplexer #(.select(5), .width(32)) multiplexer_2 (
    .in0({32{1'b0}}), .in1(ra_q), .in2(sp_q), .in3(gp_q), .in4(tp_q), .in5(t0_q), .in6(t1_q), .in7(t2_q),
    .in8(s0_q), .in9(s1_q), .in10(a0_q), .in11(a1_q), .in12(a2_q), .in13(a3_q), .in14(a4_q), .in15(a5_q),
    .in16(a6_q), .in17(a7_q), .in18(s2_q), .in19(s3_q), .in20(s4_q), .in21(s5_q), .in22(s6_q), .in23(s7_q),
    .in24(s8_q), .in25(s9_q), .in26(s10_q), .in27(s11_q), .in28(t3_q), .in29(t4_q), .in30(t5_q), .in31(t6_q),
    .out(rs1_data), .sel(rs1_index));
  Multiplexer #(.select(5), .width(32)) multiplexer_3 (
    .in0({32{1'b0}}), .in1(ra_q), .in2(sp_q), .in3(gp_q), .in4(tp_q), .in5(t0_q), .in6(t1_q), .in7(t2_q),
    .in8(s0_q), .in9(s1_q), .in10(a0_q), .in11(a1_q), .in12(a2_q), .in13(a3_q), .in14(a4_q), .in15(a5_q),
    .in16(a6_q), .in17(a7_q), .in18(s2_q), .in19(s3_q), .in20(s4_q), .in21(s5_q), .in22(s6_q), .in23(s7_q),
    .in24(s8_q), .in25(s9_q), .in26(s10_q), .in27(s11_q), .in28(t3_q), .in29(t4_q), .in30(t5_q), .in31(t6_q),
    .out(rs2_data), .sel(rs2_index));

  // Other names for the same wires on the sheet: R = Reset; rd_index2_0[2:0] = rd_index[2:0];
  //   rd_index4_3[1:0] = rd_index[4:3]

  // Notes on the sheet:
  //   zero
endmodule

module ALU (
  input  [31:0] rs1_val,
  input  [31:0] rs2_val,
  input  [31:0] imm_out,
  input  ALUSrc,
  input  [3:0] ALUop,
  output [31:0] Result,
  output zero,
  output Lt,
  output Ltu
);

  wire [31:0] adder_1_out, and_1_out, bit_extender_1_out, bit_extender_2_out, or_1_out, rs2_or_imm,
       shifter_1_out, shifter_2_out, shifter_3_out, subtractor_1_out, xor_1_out;

  Multiplexer #(.width(32)) multiplexer_1 (.in0(rs2_val), .in1(imm_out), .out(rs2_or_imm), .sel(ALUSrc));
  Comparator #(.width(32)) comparator_1 (.a(rs1_val), .b(rs2_or_imm), .lt(Lt));  // open: gt, eq
  Comparator #(.mode("unsigned"), .width(32)) comparator_2 (.a(rs1_val), .b(rs2_or_imm), .lt(Ltu));  // open: gt, eq
  Adder #(.width(32)) adder_1 (.a(rs1_val), .b(rs2_or_imm), .out(adder_1_out));  // open: cin, cout
  Subtractor #(.width(32)) subtractor_1 (.a(rs1_val), .b(rs2_or_imm), .out(subtractor_1_out));  // open: bin, bout
  Shifter #(.width(32)) shifter_1 (.in(rs1_val), .\dist (rs2_or_imm[4:0]), .out(shifter_1_out));
  assign bit_extender_1_out = {{31{1'b0}}, Lt};  // Bit_Extender bit_extender_1
  assign bit_extender_2_out = {{31{1'b0}}, Ltu};  // Bit_Extender bit_extender_2
  assign xor_1_out = rs1_val ^ rs2_or_imm;  // XOR_Gate xor_1, 32 bits wide
  Shifter #(.shift("lr"), .width(32)) shifter_2 (.in(rs1_val), .\dist (rs2_or_imm[4:0]), .out(shifter_2_out));
  Shifter #(.shift("ar"), .width(32)) shifter_3 (.in(rs1_val), .\dist (rs2_or_imm[4:0]), .out(shifter_3_out));
  assign or_1_out = rs1_val | rs2_or_imm;  // OR_Gate or_1, 32 bits wide
  assign and_1_out = rs1_val & rs2_or_imm;  // AND_Gate and_1, 32 bits wide
  Multiplexer #(.select(4), .width(32)) multiplexer_2 (
    .in0(adder_1_out), .in1(subtractor_1_out), .in2(shifter_1_out), .in3(bit_extender_1_out),
    .in4(bit_extender_2_out), .in5(xor_1_out), .in6(shifter_2_out), .in7(shifter_3_out), .in8(or_1_out),
    .in9(and_1_out), .in10(rs2_or_imm), .in11(rs1_val), .out(Result), .sel(ALUop));  // open: in12, in13, in14, in15
  Comparator #(.width(32)) comparator_3 (.a(Result), .b({32{1'b0}}), .eq(zero));  // open: gt, lt

  // Other names for the same wires on the sheet: shamt[4:0] = rs2_or_imm[4:0]

  // Notes on the sheet:
  //   SLT-0011
  //   SLTU-0100
  //   XOR-0101
  //   SRL-0110
  //   SRA-0111
  //   OR-1000
  //   AND-1001
  //   COPY-B-1010
  //   PASS-A-1011
  //   ADD-0000
  //   SUB-0001
  //   SLL-0010
endmodule

module CU (
  input  [31:0] instruction,
  input  [13:0] in_2,
  output [3:0] out_3,
  output [11:0] control_word
);

  wire [1:0] word_data;

  // Probe on instruction[6:0]
  // Probe on instruction[14:12]
  // Probe on instruction[30]
  // Probe on instruction[6:0]
  ROM #(.addrWidth(7), .dataWidth(14)) word (.addr(instruction[6:0]), .data({control_word, word_data}));
  // Probe on {control_word, word_data}
  // Probe on {control_word, word_data}
  // Probe on word_data
  ROM #(.addrWidth(6), .dataWidth(4)) ALUControl (
    .addr({word_data, instruction[30], instruction[14:12]}), .data(out_3));

  // Other names for the same wires on the sheet: funct3[2:0] = instruction[14:12]; funct7_bit = instruction[30];
  //   opcode[6:0] = instruction[6:0]

  // Notes on the sheet:
  //   contents of word (hex, n*v repeats v):
  //   0 0 0 3301 15*0 2101 0 0 0 210c 11*0 905 15*0 2000 0 0 0 210f 43*0 8a 0 0 0 2520 7*0 2451
  //   contents of ALUControl (hex, n*v repeats v):
  //   0 2 3 4 5 6 8 9 1 2 3 4 5 7 8 9 0 2 0 4 5 6 8 9 0 2 3 4 5 7 8 9 16*1
endmodule

module DataMem (
  input  [31:0] addr_in,
  input  Reset,
  input  [31:0] raw,
  input  MemWrite,
  input  MemRead,
  input  clk,
  input  [31:0] write_data,
  input  [2:0] funct3,
  output R,
  output [7:0] addr,
  output [31:0] raw_read_data,
  output mw,
  output mr,
  output ck,
  output [31:0] write_data_out,
  output [31:0] read_data
);

  wire [4:0] bit_extender_1_out, shift_amt;
  wire [31:0] LB, LBU, LH, LHU, shifter_2_out, shifter_3_out, shifter_4_out;

  assign bit_extender_1_out = {{3{1'b0}}, addr_in[1:0]};  // Bit_Extender bit_extender_1
  Shifter #(.width(5)) shifter_1 (.in(bit_extender_1_out), .\dist (3'b011), .out(shift_amt));
  Shifter #(.shift("lr"), .width(32)) shifter_2 (.in(raw), .\dist (shift_amt), .out(shifter_2_out));
  Shifter #(.width(32)) shifter_3 (.in(LBU), .\dist (5'b11000), .out(shifter_3_out));
  Shifter #(.width(32)) shifter_4 (.in(LHU), .\dist (5'b10000), .out(shifter_4_out));
  assign LBU = 32'hff & shifter_2_out;  // AND_Gate and_1, 32 bits wide
  assign LHU = 32'hffff & shifter_2_out;  // AND_Gate and_2, 32 bits wide
  Shifter #(.shift("ar"), .width(32)) shifter_5 (.in(shifter_3_out), .\dist (5'b11000), .out(LB));
  Shifter #(.shift("ar"), .width(32)) shifter_6 (.in(shifter_4_out), .\dist (5'b10000), .out(LH));
  Multiplexer #(.select(3), .width(32)) multiplexer_1 (
    .in0(LB), .in1(LH), .in2(raw), .in3({32{1'b0}}), .in4(LBU), .in5(LHU), .in6({32{1'b0}}),
    .in7({32{1'b0}}), .out(read_data), .sel(funct3));

  assign addr = addr_in[9:2];
  assign ck = clk;
  assign mr = MemRead;
  assign mw = MemWrite;
  assign R = Reset;
  assign raw_read_data = raw;
  assign write_data_out = write_data;

  // Other names for the same wires on the sheet: offset[1:0] = addr_in[1:0]; LW[31:0] = raw
endmodule

module test (
);

  wire ALUSrc, Branch, branch_taken, clk, Lt, multiplexer_3_out, not_1_out, not_2_out, reset, zero;
  wire [2:0] funct3;
  wire [3:0] ALUop;
  wire [9:2] undriven;
  wire [11:0] control_word;
  wire [31:0] alu_result, imm_b, imm_i, imm_j, imm_out, instruction, multiplexer_1_out, multiplexer_2_out,
       PC_plus_4, ram_read_data, rs1_val, rs2_val;

  // PC pc_1: pin names not known; wires that end beside it: branch_taken, imm_b, imm_j, rs1_val, imm_i, reset, control_word[4], clk, control_word[3], PC_plus_4
  ROM #(.dataWidth(32)) rom_1 (.addr(undriven), .data({instruction[31:15], funct3, instruction[11:0]}));
  Button button_1 ();  // open: out
  Clock clock_1 (.out(clk));
  Button button_2 (.out(reset));
  Multiplexer #(.width(32)) multiplexer_1 (.in0(rs2_val), .in1(imm_out), .out(multiplexer_1_out), .sel(ALUSrc));
  // Probe on rs1_val
  // ALU alu_1: pin names not known; wires that end beside it: rs1_val, multiplexer_1_out, ALUop, Lt, alu_result, zero
  // Probe on ALUop
  // Probe on multiplexer_1_out
  Multiplexer #(.select(2), .width(32)) multiplexer_2 (
    .in0(alu_result), .in1(ram_read_data), .in2(PC_plus_4), .in3({32{1'b0}}), .out(multiplexer_2_out),
    .sel(control_word[8:7]));
  // Probe on control_word[8:7]
  CU cu_1 (
    .instruction({instruction[31:15], funct3, instruction[11:0]}), .out_3(ALUop),
    .control_word({control_word[11:7], ALUSrc, Branch, control_word[4:0]}));  // open: in_2
  // RegFile regfile_1: pin names not known; wires that end beside it: instruction[19:15], reset, instruction[24:20], instruction[11:7], control_word[11], multiplexer_2_out, clk, rs2_val, rs1_val
  // Probe on multiplexer_2_out
  // Probe on rs1_val
  // Probe on alu_result
  // DataMem datamem_1: pin names not known; wires that end beside it: alu_result, rs2_val, control_word[9], control_word[10], clk, funct3, reset, ram_read_data
  // Probe on ram_read_data
  not not_1 (not_1_out, Lt);
  not not_2 (not_2_out, zero);
  Multiplexer #(.select(3)) multiplexer_3 (
    .in0(zero), .in1(not_2_out), .in2(1'b0), .in3(1'b0), .in4(Lt), .in5(not_1_out), .in6(1'b0), .in7(1'b0),
    .out(multiplexer_3_out), .sel(funct3));
  and and_1 (branch_taken, multiplexer_3_out, Branch);
  // ImmGen immgen_1: pin names not known; wires that end beside it: {instruction[31:15], funct3, instruction[11:0]}, control_word[2:0], imm_out, imm_j, imm_i, imm_b
  // Probe on imm_out

  // Other names for the same wires on the sheet: immSel[2:0] = control_word[2:0]; jalr = control_word[3];
  //   jal = control_word[4]; control_word[6:5] = {ALUSrc, Branch}; MemToReg[1:0] = control_word[8:7];
  //   MemWrite = control_word[9]; MemRead = control_word[10]; RegWrite = control_word[11];
  //   rd_index[4:0] = instruction[11:7]; instruction[14:12] = funct3; rs1_index[4:0] = instruction[19:15];
  //   rs2_index[4:0] = instruction[24:20]

  // Notes on the sheet:
  //   contents of rom_1 (hex, n*v repeats v):
  //   293 313 a00393 728c63 530333 128293 ff5ff06f 13
  //   Control Word
  //   bit 11 (RegWrite)
  //   bit 10 (MemRead)
  //   bit 9 (MemWrite)
  //   bits 8..7 (MemToReg[1:0])
  //   bit 6 (ALUSrc)
  //   bit 5 (Branch)
  //   bit 4 (Jump(JAL))
  //   bit 3 (Jalr)
  //   bits 2..0 (ImmSel[2:0])
endmodule
